# Fritzing sketch 28BYJ-48-driver_and_motor(2) (saved by Fritzing 0.9.8b)

parts:
  Motor_Driver = 28BYJ-48 Driver Module [part_number=ULN2003 package=THT]
  Stepper_Motor_for_Movement = 28BYJ-48 Stepper Motor [part_number=28BYJ-48]
  Power_plug1 = Power plug
  Controller = DOIT Esp32 DevKit v1 (30 pins long, 11 pins width) [part_number=ESP32S-PIN30]
  Pot_for_motor_RPM = POT [package=alps_pot]

nets:
  N1: Motor_Driver.IN1, Controller.D13
  N2: Motor_Driver.IN2, Controller.D12
  N3: Motor_Driver.IN3, Controller.D14
  N4: Motor_Driver.IN4, Controller.D27
  GND: Motor_Driver.GND, Power_plug1.GND
  N5: Motor_Driver.Vmotor, Power_plug1.VCC
  N6: Motor_Driver.blue-pin, Stepper_Motor_for_Movement.blue-pin
  N7: Motor_Driver.pink-pin, Stepper_Motor_for_Movement.pink-pin
  N8: Motor_Driver.yellow-pin, Stepper_Motor_for_Movement.yellow-pin
  N9: Motor_Driver.orange-pin, Stepper_Motor_for_Movement.orange-pin
  N10: Motor_Driver.red-pin, Stepper_Motor_for_Movement.red-pin
  N11: Controller.3V3, Pot_for_motor_RPM.A
  N12: Controller.GND, Pot_for_motor_RPM.E
  N13: Controller.D34, Pot_for_motor_RPM.S

custom parts:
  28BYJ-48 Driver Module: ULN2003 Driver Module for the 28BYJ-48 Unipolar Stepper Motor LED A - Blue wire - Bottom coil left LED B - Pink wire - Top coil left LED C - Yellow wire - Bottom coil right LED D - Orange wire - Top coil right Common rail - red Connector pins: blue - pink - yellow - orange - red Control pins - IN1 to IN4 Power pins - GND & Vmotor (5-12V) On/Off jumper (if removed, power to motor is cut).
  28BYJ-48 Stepper Motor: Unipolar Stepper Motor 28BYJ-48 Top coil - pink & orange Bottom coil - blue & yellow Common rail - red Connector pins: blue - pink - yellow - orange - red
  DOIT Esp32 DevKit v1 (30 pins long, 11 pins width): The DOIT Esp32 DevKit v1 is one of the development board created by DOIT to evaluate the ESP-WROOM-32 module. It is based on the ESP32 microcontroller that boasts Wifi, Bluetooth, Ethernet and Low Power support all in a single chip. (vanepp) made breadboard work, adjusted pin numbering and labels and reduced size of schematic and cleaned up pcb. This chip is 30pins long (2 x15) and 11 pins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
